// Logisim project schematic.circ as structural Verilog: 11 circuits, main circuit main
module main (
);

  alu16 alu16_1 ();  // open: Cin, B, A, S, M, Cout, O
endmodule

module alu4 (
  input  [3:0] INA,
  input  [3:0] INB,
  input  Cin,
  input  M,
  input  [3:0] S,
  output y,
  output Co,
  output x,
  output eq,
  output [3:0] F
);

  // _74181 74181_1: pin names not known; wires that end beside it: INB[0], INA[0], S[3], S[2], S[1], S[0], Cin, M, F[0], F[1], F[2], INA[1], INB[1], INA[2], INB[2], INA[3], INB[3], y, Co, x, eq, F[3]

  // Other names for the same wires on the sheet: A0 = INA[0]; A1 = INA[1]; A2 = INA[2]; A3 = INA[3]; B0 = INB[0];
  //   B1 = INB[1]; B2 = INB[2]; B3 = INB[3]
endmodule

module alu16 (
  input  Cin,
  input  [15:0] B,
  input  [15:0] A,
  input  [3:0] S,
  input  M,
  output Cout,
  output [15:0] O
);

  wire alu4_4_co, and_1_out, and_2_out, and_3_out, and_4_out, Cnx, Cny, Cnz, n7408_1_pin3, n7408_1_pin6,
       n7408_1_pin11, n7411_1_pin8, n7411_1_pin12, not_2_out, X0, X1, X2, Y0, Y1, Y2;

  alu4 alu4_1 (.INA(A[3:0]), .INB(B[3:0]), .Cin(Cin), .M(M), .S(S), .y(Y0), .x(X0), .F(O[3:0]));  // open: Co, eq
  alu4 alu4_2 (.INA(A[7:4]), .INB(B[7:4]), .Cin(Cnx), .M(M), .S(S), .y(Y1), .x(X1), .F(O[7:4]));  // open: Co, eq
  alu4 alu4_3 (.INA(A[11:8]), .INB(B[11:8]), .Cin(Cny), .M(M), .S(S), .y(Y2), .x(X2), .F(O[11:8]));  // open: Co, eq
  alu4 alu4_4 (
    .INA(A[15:12]), .INB(B[15:12]), .Cin(Cnz), .M(M), .S(S), .Co(alu4_4_co), .F(O[15:12]));  // open: y, x, eq
  not not_1 (Cout, alu4_4_co);
  not not_2 (not_2_out, Cin);
  _7411 #(.ShowInternalStructure("true")) u_7411_1 (
    .pin1(Y1), .pin2(Y0), .pin13(X0), .pin12(n7411_1_pin12), .pin11(not_2_out), .pin10(Y1), .pin9(Y0),
    .pin8(n7411_1_pin8));  // open: pin3, pin4, pin5, pin6
  and and_1 (and_1_out, not_2_out, Y0, Y1, Y2);
  and and_2 (and_2_out, X0, Y2, Y1, Y0);
  and and_3 (and_3_out, X1, Y2, Y1);
  and and_4 (and_4_out, X2, Y2);
  _7408 #(.ShowInternalStructure("true")) u_7408_1 (
    .pin1(Y0), .pin2(not_2_out), .pin3(n7408_1_pin3), .pin4(X0), .pin5(Y0), .pin6(n7408_1_pin6), .pin13(Y1),
    .pin12(X1), .pin11(n7408_1_pin11), .pin10(X2), .pin9(Y2));  // open: pin8
  _7402 #(.ShowInternalStructure("true")) u_7402_1 (
    .pin10(Cnx), .pin9(n7408_1_pin6), .pin8(n7408_1_pin3));  // open: pin1, pin2, pin3, pin4, pin5, pin6, pin13, pin12, pin11
  nor nor_1 (Cnz, and_1_out, and_2_out, and_3_out, and_4_out);
  _7427 #(.ShowInternalStructure("true")) u_7427_1 (
    .pin3(n7411_1_pin8), .pin4(n7411_1_pin12), .pin5(n7408_1_pin11), .pin6(Cny));  // open: pin1, pin2, pin13, pin12, pin11, pin10, pin9, pin8
  _7464 u_7464_1 ();  // open: pin1, pin2, pin3, pin4, pin5, pin6, pin13, pin12, pin11, pin10, pin9, pin8

  // Other names for the same wires on the sheet: Cn = Cin
endmodule

module mem (
  input  GR,
  input  [15:0] GADDR,
  input  [15:0] CDATAIN,
  input  SEL,
  input  [15:0] CPU_ADDR,
  input  CR,
  input  in_7,
  input  CW,
  input  RSE,
  input  in_10,
  output [15:0] GDATAOUT0,
  output [15:0] CDATAOUT
);

  wire not_1_out, not_2_out, or_1_out, or_2_out, or_3_out, or_4_out, or_5_out;

  or or_1 (or_1_out, CR, not_1_out);
  not not_1 (not_1_out, RSE);
  or or_2 (or_2_out, not_2_out, RSE, CR);
  or or_3 (or_3_out, not_2_out, RSE, CW);
  not not_2 (not_2_out, CPU_ADDR[15]);
  or or_4 (or_4_out, CPU_ADDR[15], RSE, CW);
  or or_5 (or_5_out, CPU_ADDR[15], RSE, CR);
  IS61 is61_1 (.ADDR(CPU_ADDR[14:0]), .WE(or_4_out), .OE(or_5_out), .DIN(CDATAIN), .DOUT(CDATAOUT));
  double_buffer double_buffer_1 (
    .ADDR0(CPU_ADDR), .ADDR1(GADDR), .R1(GR), .R0(or_2_out), .W1(in_7), .W0(or_3_out), .SEL(SEL),
    .DATAIN0(CDATAIN), .DATAOUT0(CDATAOUT), .DATAOUT1(GDATAOUT0));  // open: DATAIN1
  SST39SF010A sst39sf010a_1 (.ADDR({in_10, CPU_ADDR}), .OE(or_1_out), .DOUT(CDATAOUT[7:0]));
  SST39SF010A sst39sf010a_2 (.ADDR({in_10, CPU_ADDR}), .OE(or_1_out), .DOUT(CDATAOUT[15:8]));
endmodule

module IS61 (
  input  [15:0] DIN,
  input  [14:0] ADDR,
  input  WE,
  input  OE,
  output [15:0] DOUT
);

  wire and_1_out, not_1_out, not_2_out;
  wire [15:0] controlled_buffer_1_out;

  not not_1 (not_1_out, OE);
  RAM #(.addrWidth(15), .dataWidth(16), .databus("bidir"), .trigger("high")) ram_1 (
    .addr(ADDR), .we(not_2_out), .oe(and_1_out));  // open: clk, data
  not not_2 (not_2_out, WE);
  and and_1 (and_1_out, WE, not_1_out);
  assign controlled_buffer_1_out = not_2_out ? DIN : 16'bz;  // Controlled_Buffer controlled_buffer_1
  assign DOUT = and_1_out ? controlled_buffer_1_out : 16'bz;  // Controlled_Buffer controlled_buffer_2
endmodule

module dbel (
  input  SEL,
  input  [15:0] ADDR0,
  input  [15:0] ADDR1,
  input  R1,
  input  R0,
  input  W1,
  input  W0,
  input  [15:0] DATAIN0,
  input  [15:0] DATAIN1,
  output [15:0] DATAOUT0,
  output [15:0] DATAOUT1
);

  wire and_1_out, and_2_out, E0, E1, not_1_out, not_2_out, not_3_out, not_4_out, R, W;
  wire [15:0] ADDR, bidirectional_buffer16_2_b_out, controlled_buffer_1_out, is61_1_dout;

  not not_1 (not_1_out, SEL);
  buffer16 buffer16_1 (.A(ADDR0), .OE(SEL), .B(ADDR));
  buffer16 buffer16_2 (.A(ADDR1), .OE(not_1_out), .B(ADDR));
  IS61 is61_1 (.ADDR(ADDR[14:0]), .WE(W), .OE(R), .DIN(is61_1_dout), .DOUT(is61_1_dout));
  Multiplexer multiplexer_1 (.in0(W0), .in1(W1), .out(W), .sel(SEL));
  Multiplexer multiplexer_2 (.in0(R0), .in1(R1), .out(R), .sel(SEL));
  assign controlled_buffer_1_out = not_2_out ? DATAIN0 : 16'bz;  // Controlled_Buffer controlled_buffer_1
  bidirectional_buffer16 bidirectional_buffer16_1 (
    .OE(E0), .DIR(W0), .A_IN(is61_1_dout), .B_IN(controlled_buffer_1_out), .B_OUT(controlled_buffer_1_out),
    .A_OUT(is61_1_dout));
  not not_2 (not_2_out, W0);
  bidirectional_buffer16 bidirectional_buffer16_2 (
    .OE(E1), .DIR(W1), .A_IN(is61_1_dout), .B_IN(bidirectional_buffer16_2_b_out),
    .B_OUT(bidirectional_buffer16_2_b_out), .A_OUT(is61_1_dout));
  and and_1 (and_1_out, R1, W1);
  and and_2 (and_2_out, R0, W0);
  assign DATAOUT0 = W0 ? controlled_buffer_1_out : 16'bz;  // Controlled_Buffer controlled_buffer_2
  assign bidirectional_buffer16_2_b_out = not_3_out ? DATAIN1 : 16'bz;  // Controlled_Buffer controlled_buffer_3
  assign DATAOUT1 = W1 ? bidirectional_buffer16_2_b_out : 16'bz;  // Controlled_Buffer controlled_buffer_4
  not not_3 (not_3_out, W1);
  not not_4 (not_4_out, SEL);
  or or_1 (E0, SEL, and_2_out);
  or or_2 (E1, and_1_out, not_4_out);
endmodule

module buffer16 (
  input  [15:0] A,
  input  OE,
  output [15:0] B
);

  wire not_1_out;

  not not_1 (not_1_out, OE);
  assign B = not_1_out ? A : 16'bz;  // Controlled_Buffer controlled_buffer_1

  // Notes on the sheet:
  //   OE: pull=up
endmodule

module buffer15 (
  input  [14:0] A,
  input  OE,
  output [14:0] B
);

  wire not_1_out;

  assign B = not_1_out ? A : 15'bz;  // Controlled_Buffer controlled_buffer_1
  not not_1 (not_1_out, OE);
endmodule

module double_buffer (
  input  [15:0] DATAIN1,
  input  [15:0] DATAIN0,
  input  SEL,
  input  [15:0] ADDR0,
  input  [15:0] ADDR1,
  input  R1,
  input  R0,
  input  W1,
  input  W0,
  output [15:0] DATAOUT0,
  output [15:0] DATAOUT1
);

  wire not_1_out;

  not not_1 (not_1_out, SEL);
  dbel dbel_1 (
    .SEL(SEL), .ADDR0(ADDR0), .ADDR1(ADDR1), .R1(R1), .R0(R0), .W1(W1), .W0(W0), .DATAIN0(DATAIN0),
    .DATAIN1(DATAIN1), .DATAOUT0(DATAOUT0), .DATAOUT1(DATAOUT1));
  dbel dbel_2 (
    .SEL(not_1_out), .ADDR0(ADDR0), .ADDR1(ADDR1), .R1(R1), .R0(R0), .W1(W1), .W0(W0), .DATAIN0(DATAIN0),
    .DATAIN1(DATAIN1), .DATAOUT0(DATAOUT0), .DATAOUT1(DATAOUT1));
endmodule

module bidirectional_buffer16 (
  input  DIR,
  input  OE,
  input  [15:0] A_IN,
  input  [15:0] B_IN,
  output [15:0] B_OUT,
  output [15:0] A_OUT
);

  wire and_1_out, and_2_out, not_1_out, not_2_out;

  not not_1 (not_1_out, OE);
  not not_2 (not_2_out, DIR);
  and and_1 (and_1_out, not_2_out, not_1_out);
  assign A_OUT = and_1_out ? B_IN : 16'bz;  // Controlled_Buffer controlled_buffer_1
  and and_2 (and_2_out, DIR, not_1_out);
  assign B_OUT = and_2_out ? A_IN : 16'bz;  // Controlled_Buffer controlled_buffer_2
endmodule

module SST39SF010A (
  input  [16:0] ADDR,
  input  OE,
  output [7:0] DOUT
);

  wire not_1_out;
  wire [7:0] rom_1_data;

  ROM #(.addrWidth(17)) rom_1 (.addr(ADDR), .data(rom_1_data));
  assign DOUT = not_1_out ? rom_1_data : 8'bz;  // Controlled_Buffer controlled_buffer_1
  not not_1 (not_1_out, OE);

  // Notes on the sheet:
  //   contents of rom_1 (hex, n*v repeats v):
  //   4
endmodule
