// Digital circuit ctrl.dig as structural Verilog
module ctrl (
  input  IRI,
  input  [15:0] IRDI,
  input  CLK,
  output nMW,
  output nMR,
  output MSL,
  output nMAL,
  output IRIC,
  output [2:0] RSEL,
  output nRGI,
  output nRGO,
  output nIN_ALA,
  output nIN_ALB,
  output [3:0] ALF,
  output nALO,
  output PCE,
  output nPCL,
  output nPCO,
  output HLT,
  output nMCR,
  output SWP,
  output JNZ
);

  wire _74161_1_pin2, _74161_1_pin3;
  wire [3:0] _74161_1_pin14;
  wire [15:0] reg16_1_dout;

  _74161 _74161_1 (
    .pin1(nMCR), .pin2(_74161_1_pin2), .pin3(_74161_1_pin3), .pin4(_74161_1_pin3), .pin5(_74161_1_pin3),
    .pin6(_74161_1_pin3), .pin7(1'b1), .pin8(1'b0), .pin9(1'b1), .pin10(1'b1), .pin11(_74161_1_pin14[3]),
    .pin12(_74161_1_pin14[2]), .pin13(_74161_1_pin14[1]), .pin14(_74161_1_pin14[0]), .pin16(1'b1));  // open: pin15
  reg16 reg16_1 (.nWE(IRI), .CLK(CLK), .DIN(IRDI), .nOE(1'b0), .DOUT(reg16_1_dout));
  not not_1 (_74161_1_pin2, CLK);
  // NotConnected on _74161_1_pin3
  // Probe on {reg16_1_dout[13:0], _74161_1_pin14}
  ROM #(.AddrBits(18), .Bits(24)) rom_1 (
    .A({reg16_1_dout[13:0], _74161_1_pin14}), .sel(1'b1),
    .D({JNZ, SWP, nMCR, HLT, nPCO, nPCL, PCE, nALO, ALF, nIN_ALB, nIN_ALA, nRGO, nRGI, RSEL, IRIC, nMAL, MSL, nMR, nMW}));

  // Notes on the sheet:
  //   contents of rom_1 (hex, n*v repeats v):
  //   250f13,2f0f0d,510*2d0f1b,250f13,2f0f0d,250f13,2f0b1d,2d051b,2c2e1b
  //   ,d0f1b,313*2d0f1b,250f13,2f0f0d,250f13,2f071d,2d09d3,2cff1a,2c8edb
  //   ,d0f1b,8*2d0f1b,250f13,2f0f0d,250f13,2f0f15,2d0719,2d09d3,2cff1a
  //   ,2c8edb,d0f1b,39*2d0f1b,250f13,2f0f0d,2d091b,2d051b,2c2e1b,d0f1b
  //   ,10*2d0f1b,250f13,2f0f0d,2d093b,2d051b,2c2e1b,d0f1b,10*2d0f1b
  //   ,250f13,2f0f0d,2d095b,2d051b,2c2e1b,d0f1b,10*2d0f1b,250f13,2f0f0d
  //   ,2d097b,2d051b,2c2e1b,d0f1b,10*2d0f1b,250f13,2f0f0d,2d099b,2d051b
  //   ,2c2e1b,d0f1b,10*2d0f1b,250f13,2f0f0d,2d09bb,2d051b,2c2e1b,d0f1b
  //   ,10*2d0f1b,250f13,2f0f0d,2d09db,2d051b,2c2e1b,d0f1b,10*2d0f1b
  //   ,250f13,2f0f0d,2d09fb,2d051b,2c2e1b,d0f1b,522*2d0f1b,250f13,2f0f0d
  //   ,250f13,2f0b1d,2d053b,2c2e3b,d0f1b,377*2d0f1b,250f13,2f0f0d,2d091b
  //   ,2d053b,2c2e3b,d0f1b,10*2d0f1b,250f13,2f0f0d,2d093b,2d053b,2c2e3b
  //   ,d0f1b,10*2d0f1b,250f13,2f0f0d,2d095b,2d053b,2c2e3b,d0f1b,10*2d0f1b
  //   ,250f13,2f0f0d,2d097b,2d053b,2c2e3b,d0f1b,10*2d0f1b,250f13,2f0f0d
  //   ,2d099b,2d053b,2c2e3b,d0f1b,10*2d0f1b,250f13,2f0f0d,2d09bb,2d053b
  //   ,2c2e3b,d0f1b,10*2d0f1b,250f13,2f0f0d,2d09db,2d053b,2c2e3b,d0f1b
  //   ,10*2d0f1b,250f13,2f0f0d,2d09fb,2d053b,2c2e3b,d0f1b,522*2d0f1b
  //   ,250f13,2f0f0d,250f13,2f0b1d,2d055b,2c2e5b,d0f1b,377*2d0f1b,250f13
  //   ,2f0f0d,2d091b,2d055b,2c2e5b,d0f1b,10*2d0f1b,250f13,2f0f0d,2d093b
  //   ,2d055b,2c2e5b,d0f1b,10*2d0f1b,250f13,2f0f0d,2d095b,2d055b,2c2e5b
  //   ,d0f1b,10*2d0f1b,250f13,2f0f0d,2d097b,2d055b,2c2e5b,d0f1b,10*2d0f1b
  //   ,250f13,2f0f0d,2d099b,2d055b,2c2e5b,d0f1b,10*2d0f1b,250f13,2f0f0d
  //   ,2d09bb,2d055b,2c2e5b,d0f1b,10*2d0f1b,250f13,2f0f0d,2d09db,2d055b
  //   ,2c2e5b,d0f1b,10*2d0f1b,250f13,2f0f0d,2d09fb,2d055b,2c2e5b,d0f1b
  //   ,522*2d0f1b,250f13,2f0f0d,250f13,2f0b1d,2d057b,2c2e7b,d0f1b,377*2d0f1b
  //   ,250f13,2f0f0d,2d091b,2d057b,2c2e7b,d0f1b,10*2d0f1b,250f13,2f0f0d
  //   ,2d093b,2d057b,2c2e7b,d0f1b,10*2d0f1b,250f13,2f0f0d,2d095b,2d057b
  //   ,2c2e7b,d0f1b,10*2d0f1b,250f13,2f0f0d,2d097b,2d057b,2c2e7b,d0f1b
  //   ,10*2d0f1b,250f13,2f0f0d,2d099b,2d057b,2c2e7b,d0f1b,10*2d0f1b
  //   ,250f13,2f0f0d,2d09bb,2d057b,2c2e7b,d0f1b,10*2d0f1b,250f13,2f0f0d
  //   ,2d09db,2d057b,2c2e7b,d0f1b,10*2d0f1b,250f13,2f0f0d,2d09fb,2d057b
  //   ,2c2e7b,d0f1b,522*2d0f1b,250f13,2f0f0d,250f13,2f0b1d,2d059b,2c2e9b
  //   ,d0f1b,377*2d0f1b,250f13,2f0f0d,2d091b,2d059b,2c2e9b,d0f1b,10*2d0f1b
  //   ,250f13,2f0f0d,2d093b,2d059b,2c2e9b,d0f1b,10*2d0f1b,250f13,2f0f0d
  //   ,2d095b,2d059b,2c2e9b,d0f1b,10*2d0f1b,250f13,2f0f0d,2d097b,2d059b
  //   ,2c2e9b,d0f1b,10*2d0f1b,250f13,2f0f0d,2d099b,2d059b,2c2e9b,d0f1b
  //   ,10*2d0f1b,250f13,2f0f0d,2d09bb,2d059b,2c2e9b,d0f1b,10*2d0f1b
  //   ,250f13,2f0f0d,2d09db,2d059b,2c2e9b,d0f1b,10*2d0f1b,250f13,2f0f0d
  //   ,2d09fb,2d059b,2c2e9b,d0f1b,522*2d0f1b,250f13,2f0f0d,250f13,2f0b1d
  //   ,2d05bb,2c2ebb,d0f1b,377*2d0f1b,250f13,2f0f0d,2d091b,2d05bb,2c2ebb
  //   ,d0f1b,10*2d0f1b,250f13,2f0f0d,2d093b,2d05bb,2c2ebb,d0f1b,10*2d0f1b
  //   ,250f13,2f0f0d,2d095b,2d05bb,2c2ebb,d0f1b,10*2d0f1b,250f13,2f0f0d
  //   ,2d097b,2d05bb,2c2ebb,d0f1b,10*2d0f1b,250f13,2f0f0d,2d099b,2d05bb
  //   ,2c2ebb,d0f1b,10*2d0f1b,250f13,2f0f0d,2d09bb,2d05bb,2c2ebb,d0f1b
  //   ,10*2d0f1b,250f13,2f0f0d,2d09db,2d05bb,2c2ebb,d0f1b,10*2d0f1b
  //   ,250f13,2f0f0d,2d09fb,2d05bb,2c2ebb,d0f1b,522*2d0f1b,250f13,2f0f0d
  //   ,250f13,2f0b1d,2d05db,2c2edb,d0f1b,249*2d0f1b,250f13,2f0f0d,2d0d13
  //   ,2d0719,2d09d3,2cff1a,2c8edb,d0f1b,8*2d0f1b,250f13,2f0f0d,2d0d33
  //   ,2d0719,2d09d3,2cff1a,2c8edb,d0f1b,8*2d0f1b,250f13,2f0f0d,2d0d53
  //   ,2d0719,2d09d3,2cff1a,2c8edb,d0f1b,8*2d0f1b,250f13,2f0f0d,2d0d73
  //   ,2d0719,2d09d3,2cff1a,2c8edb,d0f1b,8*2d0f1b,250f13,2f0f0d,2d0d93
  //   ,2d0719,2d09d3,2cff1a,2c8edb,d0f1b,8*2d0f1b,250f13,2f0f0d,2d0db3
  //   ,2d0719,2d09d3,2cff1a,2c8edb,d0f1b,8*2d0f1b,250f13,2f0f0d,2d0dd3
  //   ,2d0719,2d09d3,2cff1a,2c8edb,d0f1b,8*2d0f1b,250f13,2f0f0d,2d0df3
  //   ,2d0719,2d09d3,2cff1a,2c8edb,d0f1b,8*2d0f1b,250f13,2f0f0d,2d091b
  //   ,2d05db,2c2edb,d0f1b,10*2d0f1b,250f13,2f0f0d,2d093b,2d05db,2c2edb
  //   ,d0f1b,10*2d0f1b,250f13,2f0f0d,2d095b,2d05db,2c2edb,d0f1b,10*2d0f1b
  //   ,250f13,2f0f0d,2d097b,2d05db,2c2edb,d0f1b,10*2d0f1b,250f13,2f0f0d
  //   ,2d099b,2d05db,2c2edb,d0f1b,10*2d0f1b,250f13,2f0f0d,2d09bb,2d05db
  //   ,2c2edb,d0f1b,10*2d0f1b,250f13,2f0f0d,2d09db,2d05db,2c2edb,d0f1b
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endmodule
