// Digital circuit gpu.dig as structural Verilog
module gpu (
  input  PC,
  input  [15:0] VDATA,
  output [3:0] R,
  output [3:0] G,
  output [3:0] B,
  output HSYNC,
  output VSYNC,
  output [14:0] VADDR,
  output nVOE
);

  wire comparator_1_eq, comparator_2_eq, comparator_3_eq, comparator_4_eq, comparator_5_eq, comparator_6_eq,
       comparator_7_eq, comparator_8_eq, nOE_H, nOE_V;
  wire [10:0] counter_2_out;
  wire [11:0] counter_1_out;

  Counter #(.Bits(12)) counter_1 (
    .en(1'b1), .C(PC), .clr(comparator_3_eq), .out({counter_1_out[11], VADDR[7:0], counter_1_out[2:0]}));  // open: ovf
  Counter #(.Bits(11)) counter_2 (
    .en(1'b1), .C(comparator_3_eq), .clr(comparator_7_eq),
    .out({counter_2_out[10], VADDR[14:8], counter_2_out[2:0]}));  // open: ovf
  Comparator #(.Bits(12)) comparator_1 (
    .a({counter_1_out[11], VADDR[7:0], counter_1_out[2:0]}), .b(12'h530), .eq(comparator_1_eq));  // open: gt, lt
  Comparator #(.Bits(12)) comparator_2 (
    .a({counter_1_out[11], VADDR[7:0], counter_1_out[2:0]}), .b(12'h5a0), .eq(comparator_2_eq));  // open: gt, lt
  Comparator #(.Bits(12)) comparator_3 (
    .a({counter_1_out[11], VADDR[7:0], counter_1_out[2:0]}), .b(12'h697), .eq(comparator_3_eq));  // open: gt, lt
  Comparator #(.Bits(12)) comparator_4 (
    .a({counter_1_out[11], VADDR[7:0], counter_1_out[2:0]}), .b(12'h500), .eq(comparator_4_eq));  // open: gt, lt
  Comparator #(.Bits(11)) comparator_5 (
    .a({counter_2_out[10], VADDR[14:8], counter_2_out[2:0]}), .b(11'h401), .eq(comparator_5_eq));  // open: gt, lt
  Comparator #(.Bits(11)) comparator_6 (
    .a({counter_2_out[10], VADDR[14:8], counter_2_out[2:0]}), .b(11'h404), .eq(comparator_6_eq));  // open: gt, lt
  Comparator #(.Bits(11)) comparator_7 (
    .a({counter_2_out[10], VADDR[14:8], counter_2_out[2:0]}), .b(11'h429), .eq(comparator_7_eq));  // open: gt, lt
  Comparator #(.Bits(11)) comparator_8 (
    .a({counter_2_out[10], VADDR[14:8], counter_2_out[2:0]}), .b(11'h400), .eq(comparator_8_eq));  // open: gt, lt
  RS_FF_AS rs_ff_as_1 (.S(comparator_5_eq), .R(comparator_6_eq), .Q(VSYNC));  // open: nQ
  RS_FF_AS rs_ff_as_2 (.S(comparator_1_eq), .R(comparator_2_eq), .Q(HSYNC));  // open: nQ
  RS_FF_AS #(.Default(1)) rs_ff_as_3 (.S(comparator_3_eq), .R(comparator_4_eq), .nQ(nOE_H));  // open: Q
  RS_FF_AS #(.Default(1)) rs_ff_as_4 (.S(comparator_7_eq), .R(comparator_8_eq), .nQ(nOE_V));  // open: Q
  and and_1 (nVOE, nOE_V, nOE_H);

  assign B = VDATA[3:0];
  assign G = VDATA[7:4];
  assign R = VDATA[11:8];

  // Other names for the same wires on the sheet: VADDR_t[6:0] = VADDR[14:8]; HADDR[7:0] = VADDR[7:0]

  // Notes on the sheet:
  //   PC: Hz: 108000000
endmodule
