// Digital circuit ramchip.dig as structural Verilog
module ramchip (
  input  nWE,
  input  [15:0] D,
  input  nOE,
  input  [14:0] ADDR
);

  wire [15:0] ramasync_q;

  RAMAsync #(.AddrBits(15), .Bits(16)) ramasync (.A(ADDR), .D(D), .we(~nWE), .Q(ramasync_q));
  assign D = ~nOE ? ramasync_q : 16'bz;  // DriverInvSel driverinvsel_1
endmodule
