// Digital circuit reg4x16.dig as structural Verilog
module reg4x16 (
  input  [15:0] DIN,
  input  [1:0] ADDR,
  input  nOE,
  input  nWE,
  input  nSEL,
  input  CLK,
  output [15:0] DOUT
);

  wire and_1_out, not_1_out, not_2_out, or_1_out, or_2_out;
  wire [15:0] REGFILE_q;

  or or_1 (or_1_out, nSEL, nOE);
  or or_2 (or_2_out, nSEL, nWE);
  not not_1 (not_1_out, or_2_out);
  and and_1 (and_1_out, CLK, not_1_out);
  not not_2 (not_2_out, and_1_out);
  RAMAsync #(.Bits(16)) REGFILE (.A(ADDR), .D(DIN), .we(~not_2_out), .Q(REGFILE_q));
  assign DOUT = ~or_1_out ? REGFILE_q : 16'bz;  // DriverInvSel driverinvsel_1
endmodule
